# Fritzing sketch kamersensor-bedrading (saved by Fritzing 1.0.5)

parts:
  ESP32 = ESP32 DevKit (WROOM-32, CP2102)
  LD2450 = HLK-LD2450 radar
  BH1750 = BH1750 lichtsensor (GY-302)
  SHT31 = GY-SHT31-D temp/vocht

nets:
  N1: ESP32.GND#13, LD2450.GND
  VIN: ESP32.VIN, LD2450.5V
  N2: ESP32.D22_SCL, BH1750.SCL, SHT31.SCL
  N3: ESP32.D21_SDA, BH1750.SDA, SHT31.SDA
  N4: ESP32.TX2/17, LD2450.RX
  N5: ESP32.RX2/16, LD2450.TX
  GND: ESP32.GND#28, BH1750.GND, SHT31.GND
  3V3: ESP32.3V3, BH1750.VCC, SHT31.VIN

notes:
  Kamersensor (zelfbouw Everything Presence Lite + SHT31) - firmware esphome/kamersensor.yaml
  LD2450: 5V → VIN, GND, TX → RX2 (GPIO16), RX → TX2 (GPIO17).
  I2C: SDA → GPIO21, SCL → GPIO22, VCC → 3V3. SHT31 doorgelust via BH1750 (4 korte draadjes solderen).
  ADDR/ADR/ALR open laten (adressen 0x23 / 0x44). Voeding: micro-USB 5 V lader.

custom parts:
  ESP32 DevKit (WROOM-32, CP2102): ESP32 DevKit (WROOM-32, CP2102) - generated for the jacuzzi / kamersensor wiring drawings
  HLK-LD2450 radar: HLK-LD2450 radar - generated for the jacuzzi / kamersensor wiring drawings
  BH1750 lichtsensor (GY-302): BH1750 lichtsensor (GY-302) - generated for the jacuzzi / kamersensor wiring drawings
  GY-SHT31-D temp/vocht: GY-SHT31-D temp/vocht - generated for the jacuzzi / kamersensor wiring drawings
