# Fritzing sketch jacuzzi-bedrading (saved by Fritzing 1.0.5)

parts:
  ESP32 = ESP32 DevKit (WROOM-32, CP2102)
  Deksel = Dekselcontact MC-38 (reed)
  DS18B20_luchtsonde_1_m = DS18B20 luchtsonde 1 m
  DS18B20_watersonde_4_m = DS18B20 watersonde 4 m
  Breakout_B = Breakout B (logo)
  Breakout_A = Breakout A (EXP1)
  Spa_EXP1 = SpaNET SV3 - EXP1
  Step-down = Step-down 3,3V (MINI560)
  pull-up_luchtsonde_4k7 = Resistor [resistance=4.7k tolerance=±1% power=0.25W package=THT]
  pull-up_watersonde_4k7 = Resistor [resistance=4.7k tolerance=±1% power=0.25W package=THT]
  R1_220 = Resistor [resistance=220 tolerance=±1% power=0.25W package=THT]
  R2_220 = Resistor [resistance=220 tolerance=±1% power=0.25W package=THT]

nets:
  N1: ESP32.GND#13, Deksel.GND, DS18B20_luchtsonde_1_m.GND_(zwart), Breakout_B.bus_7, Breakout_B.klem_7
  N2: ESP32.D19, Deksel.D19
  N3: ESP32.D18, DS18B20_luchtsonde_1_m.data_(geel), pull-up_luchtsonde_4k7.Pin_0
  N4: ESP32.TX2/17, R2_220.Pin_0
  N5: ESP32.RX2/16, R1_220.Pin_0
  N6: ESP32.D4, DS18B20_watersonde_4_m.data_(geel), pull-up_watersonde_4k7.Pin_0
  N7: ESP32.GND#28, DS18B20_watersonde_4_m.GND_(zwart), Step-down.OUT-_GND
  N8: ESP32.3V3, DS18B20_luchtsonde_1_m.VCC_(rood), DS18B20_watersonde_4_m.VCC_(rood), Step-down.OUT+_3_3V, pull-up_luchtsonde_4k7.Pin_1, pull-up_watersonde_4k7.Pin_1
  N9: Breakout_B.bus_1, Breakout_B.klem_1, Breakout_A.bus_1, Breakout_A.klem_1, Spa_EXP1.1_+13V_logo
  N10: Breakout_B.bus_2, Breakout_B.klem_2, Breakout_A.bus_2, Breakout_A.klem_2, Spa_EXP1.2_logo-signaal
  N11: Breakout_A.bus_5, Breakout_A.klem_5, Spa_EXP1.5_data_(spa_TX), R1_220.Pin_1
  N12: Breakout_A.bus_6, Breakout_A.klem_6, Spa_EXP1.6_data_(spa_RX), R2_220.Pin_1
  N13: Breakout_A.bus_7, Breakout_A.klem_7, Spa_EXP1.7_GND, Step-down.IN-
  N14: Breakout_A.bus_8, Breakout_A.klem_8, Spa_EXP1.8_VIN_12-13V, Step-down.IN+

notes:
  Jacuzzi ESP32 - EXP1 (SpaNET SV3) - firmware esphome/jacuzzi.yaml
  Oranje = 3V3-rail, zwart = GND-rail (boven en onder, lopen rond de ESP32). Grijs = patchkabel EXP1 → breakout A (klem n = pin n).
  Pin 5/6 via 220 Ω (in serie) naar RX2 (GPIO16) / TX2 (GPIO17). Pin 8 → step-down (MINI560) → 3V3. Pin 7 = GND.
  Sondes: data watersonde → GPIO4, luchtsonde → GPIO18, elk met 4,7 kΩ pull-up tussen data en 3V3. Deksel (reed): GPIO19 ↔ GND.
  Logo blijft werken: klem 1 en 2 van A → B, klem 7 van B aan GND, logostekker in B.
  Eerst meten (COM op pin 7): pin 8 ≈ 12-13 V, pin 5/6 in rust ≈ 3,3 V (bij 5 V spanningsdeler op RX).

custom parts:
  ESP32 DevKit (WROOM-32, CP2102): ESP32 DevKit (WROOM-32, CP2102) - generated for the jacuzzi / kamersensor wiring drawings
  Dekselcontact MC-38 (reed): Dekselcontact MC-38 (reed) - generated for the jacuzzi / kamersensor wiring drawings
  DS18B20 luchtsonde 1 m: DS18B20 luchtsonde 1 m - generated for the jacuzzi / kamersensor wiring drawings
  DS18B20 watersonde 4 m: DS18B20 watersonde 4 m - generated for the jacuzzi / kamersensor wiring drawings
  Breakout B (logo): Breakout B (logo) - generated for the jacuzzi / kamersensor wiring drawings
  Breakout A (EXP1): Breakout A (EXP1) - generated for the jacuzzi / kamersensor wiring drawings
  SpaNET SV3 - EXP1: SpaNET SV3 - EXP1 - generated for the jacuzzi / kamersensor wiring drawings
  Step-down 3,3V (MINI560): Step-down 3,3V (MINI560) - generated for the jacuzzi / kamersensor wiring drawings
