# Fritzing sketch jacuzzi-montage (saved by Fritzing 1.0.5)

parts:
  ESP32_op_schroefklemmenbord = ESP32 DevKit (WROOM-32, CP2102)
  Wago_GND = Wago 221-415 GND
  Wago_3V3 = Wago 221-415 3V3
  Deksel = Dekselcontact MC-38
  Buitensonde = DS18B20 buitensonde 1 m
  Watersonde = DS18B20 watersonde 4 m
  Breakout_A = Breakout A (EXP1)
  Spa_EXP1 = SpaNET SV3 - EXP1
  Mini_560_PRO = Mini 560 PRO step-down 3,3 V
  Breakout_B = Breakout B (logo)
  R1_220_(in_de_draad) = Resistor [resistance=220 tolerance=±1% power=0.25W package=THT]
  R2_220_(in_de_draad) = Resistor [resistance=220 tolerance=±1% power=0.25W package=THT]

nets:
  N1: ESP32_op_schroefklemmenbord.D19, Deksel.draad_1
  N2: ESP32_op_schroefklemmenbord.D18, Buitensonde.geel_(data)
  N3: ESP32_op_schroefklemmenbord.TX2/17, R2_220_(in_de_draad).Pin_0
  N4: ESP32_op_schroefklemmenbord.RX2/16, R1_220_(in_de_draad).Pin_0
  N5: ESP32_op_schroefklemmenbord.D4, Watersonde.geel_(data)
  N6: ESP32_op_schroefklemmenbord.GND, Wago_GND.klem_1, Wago_GND.klem_2, Wago_GND.klem_3, Wago_GND.klem_4, Wago_GND.klem_5, Deksel.draad_2, Buitensonde.zwart_(GND), Watersonde.zwart_(GND), Breakout_A.bus_7, Breakout_A.klem_7, Spa_EXP1.7_GND, Mini_560_PRO.IN-_a, Mini_560_PRO.IN-_b, Mini_560_PRO.OUT-_a, Breakout_B.bus_7, Breakout_B.klem_7
  N7: ESP32_op_schroefklemmenbord.3V3, Wago_3V3.klem_1, Wago_3V3.klem_2, Wago_3V3.klem_3, Wago_3V3.klem_4, Buitensonde.rood_(3V3), Watersonde.rood_(3V3), Mini_560_PRO.OUT+_a
  N8: Breakout_A.bus_1, Breakout_A.klem_1, Spa_EXP1.1_+13V_logo, Breakout_B.bus_1, Breakout_B.klem_1
  N9: Breakout_A.bus_2, Breakout_A.klem_2, Spa_EXP1.2_logo-signaal, Breakout_B.bus_2, Breakout_B.klem_2
  N10: Breakout_A.bus_5, Breakout_A.klem_5, Spa_EXP1.5_data_(spa_TX), R1_220_(in_de_draad).Pin_1
  N11: Breakout_A.bus_6, Breakout_A.klem_6, Spa_EXP1.6_data_(spa_RX), R2_220_(in_de_draad).Pin_1
  N12: Breakout_A.bus_8, Breakout_A.klem_8, Spa_EXP1.8_VIN_12-13V, Mini_560_PRO.IN+_a

notes:
  Jacuzzi ESP32 - montage (schroefklemmenbord + Wago 221-415) - firmware esphome/jacuzzi.yaml
  Elke draad gaat in een schroefklem van het ESP32-bord of in een Wago-klem. Wago GND en Wago 3V3 zijn de 'rijen': alle 5 klemmen zijn intern verbonden.
  Pull-up 4,7 kΩ: in de sondekabel solderen tussen rood en geel, krimpkous erover. 220 Ω: in de datadraad solderen, krimpkous erover.
  Mini 560: elke aansluiting heeft 2 gaatjes (doorverbonden) - IN- b neemt de GND van het logo. IN- en OUT- zijn intern dezelfde massa.
  Nooit tegelijk USB en de Mini 560 op de ESP32. Firmware-updates gaan draadloos (OTA).

custom parts:
  ESP32 DevKit (WROOM-32, CP2102): ESP32 DevKit (WROOM-32, CP2102) - generated for the jacuzzi / kamersensor wiring drawings
  Wago 221-415 GND: Wago 221-415 GND - generated for the jacuzzi / kamersensor wiring drawings
  Wago 221-415 3V3: Wago 221-415 3V3 - generated for the jacuzzi / kamersensor wiring drawings
  Dekselcontact MC-38: Dekselcontact MC-38 - generated for the jacuzzi / kamersensor wiring drawings
  DS18B20 buitensonde 1 m: DS18B20 buitensonde 1 m - generated for the jacuzzi / kamersensor wiring drawings
  DS18B20 watersonde 4 m: DS18B20 watersonde 4 m - generated for the jacuzzi / kamersensor wiring drawings
  Breakout A (EXP1): Breakout A (EXP1) - generated for the jacuzzi / kamersensor wiring drawings
  SpaNET SV3 - EXP1: SpaNET SV3 - EXP1 - generated for the jacuzzi / kamersensor wiring drawings
  Mini 560 PRO step-down 3,3 V: Mini 560 PRO step-down 3,3 V - generated for the jacuzzi / kamersensor wiring drawings
  Breakout B (logo): Breakout B (logo) - generated for the jacuzzi / kamersensor wiring drawings
